// Digital circuit circuito 25-03-2026.dig as structural Verilog
module circuito_25_03_2026 (
  input  in_1,
  input  in_2,
  input  in_3,
  input  in_4,
  input  in_5,
  input  in_6,
  input  in_7,
  input  in_8,
  input  in_9,
  input  dia,
  input  Umido,
  input  manual,
  input  Calor
);

  wire and_1_out, not_1_out, not_2_out, or_1_out;

  not not_1 (not_1_out, Umido);
  not not_2 (not_2_out, dia);
  and and_1 (and_1_out, Calor, not_1_out, not_2_out);
  or or_1 (or_1_out, and_1_out, manual);
  LED Regar (.in(or_1_out));
  Seven_Seg seven_seg_1 (.a(in_4), .b(in_3), .c(in_2), .d(in_1), .e(in_5), .f(in_7), .g(in_8), .dp(in_9));

  assign in_6 = in_5;
endmodule
